# Fritzing sketch big-picture (saved by Fritzing 0.8.7b)
breadboards: 1

parts:
  Part2 = Arduino Pro Mini v13
  S1 = Pushbutton [package="[THT]"]
  R1 = Resistor [tolerance=±5% resistance=100 package=THT]
  NEOPIXEL1 = Neopixel Strip -- White (60/m)
  R2 = Resistor [tolerance=±5% resistance=330 package=THT]
  Raspberry_Pi_B_rev1 = Raspberry Pi B rev2
  C1 = Electrolytic Capacitor [capacitance=1mF package="100 mil [THT, electrolytic]"]
  Part3 = Arduino Pro Mini v13
  NEOPIXEL2 = Neopixel Strip -- White (60/m)
  C2 = Electrolytic Capacitor [capacitance=1mF package="100 mil [THT, electrolytic]"]
  R3 = Resistor [tolerance=±5% resistance=100 package=THT]
  S2 = Pushbutton [package="[THT]"]
  R4 = Resistor [tolerance=±5% resistance=330 package=THT]
  JACK1 = 2.1mm Barrel Jack with Terminal Block
  Part4 = Arduino Pro Mini v13
  S3 = Pushbutton [package="[THT]"]
  R5 = Resistor [tolerance=±5% resistance=100 package=THT]
  R6 = Resistor [tolerance=±5% resistance=330 package=THT]
  NEOPIXEL3 = Neopixel Strip -- White (60/m)
  C3 = Electrolytic Capacitor [capacitance=1mF package="100 mil [THT, electrolytic]"]

nets:
  VCC: Part2.VCC, S1.Pin_3, S1.Pin_4, Part3.VCC, S2.Pin_3, S2.Pin_4, Part4.VCC, S3.Pin_3, S3.Pin_4
  GND: Part2.GND, R1.Pin_1, Raspberry_Pi_B_rev1.GND, Part3.GND, R3.Pin_1, Part4.GND, R5.Pin_1
  N1: Part2.A4, Raspberry_Pi_B_rev1.GPIO_2, Part3.A4, Part4.A4
  N2: Part2.A5, Raspberry_Pi_B_rev1.GPIO_3, Part3.A5, Part4.A5
  N3: Part2.D6_PWM, R2.Pin_0
  N4: Part2.D2, S1.Pin_1, S1.Pin_2, R1.Pin_0
  N5: NEOPIXEL1.+5V, R2.Pin_1
  N6: NEOPIXEL1.DI, C1.+, NEOPIXEL2.DI, C2.+, JACK1.POS, NEOPIXEL3.DI, C3.+
  GND_2: NEOPIXEL1.GND, C1.-, NEOPIXEL2.GND, C2.-, JACK1.NEG, NEOPIXEL3.GND, C3.-
  N7: Part3.D6_PWM, R4.Pin_0
  N8: Part3.D2, R3.Pin_0, S2.Pin_1, S2.Pin_2
  N9: NEOPIXEL2.+5V, R4.Pin_1
  N10: Part4.D6_PWM, R6.Pin_0
  N11: Part4.D2, S3.Pin_1, S3.Pin_2, R5.Pin_0
  N12: R6.Pin_1, NEOPIXEL3.+5V

custom parts:
  Neopixel Strip -- White (60/m): Neopixel Strip, White, 60 pixels per meter.
