# Fritzing sketch single-strip (saved by Fritzing 0.8.7b)
circuit board: 3.5486cm x 4.95831cm
breadboards: 1

parts:
  ARDUINO_PRO_MINI = Arduino Pro Mini v13
  R2 = Resistor [tolerance=±5% resistance=330 package=THT]
  ADDRESS_SELECT = female pin header, 6 pins [form="♀ (female)"]
  ADRSEL_HIGH = female pin header, 6 pins [form="♀ (female)"]
  RASPBERRY_PI = screw terminal, 3 pins
  SWITCH = Screw terminal - 2 pins [package=THT]
  PXL/PWR = screw terminal, 3 pins
  C1 = Electrolytic Capacitor [capacitance=1mF package="100 mil [THT, electrolytic]"]
  R3 = Resistor [tolerance=±5% resistance=100 package=THT]

nets:
  N1: ARDUINO_PRO_MINI.GND, RASPBERRY_PI.pin3, PXL/PWR.pin1, C1.-, R3.Pin_1
  N2: ARDUINO_PRO_MINI.A4, RASPBERRY_PI.pin1
  N3: ARDUINO_PRO_MINI.A5, RASPBERRY_PI.pin2
  N4: ARDUINO_PRO_MINI.RAW, PXL/PWR.pin2, C1.+
  N5: ARDUINO_PRO_MINI.D11_PWM/MOSI, R2.Pin_0
  N6: ARDUINO_PRO_MINI.D9_PWM, ADDRESS_SELECT.pin6
  N7: ARDUINO_PRO_MINI.D8, ADDRESS_SELECT.pin5
  N8: ARDUINO_PRO_MINI.D7, ADDRESS_SELECT.pin4
  N9: ARDUINO_PRO_MINI.D5_PWM, ADDRESS_SELECT.pin3
  N10: ARDUINO_PRO_MINI.D4, ADDRESS_SELECT.pin2
  N11: ARDUINO_PRO_MINI.D3_PWM, ADDRESS_SELECT.pin1
  N12: ARDUINO_PRO_MINI.D2, SWITCH.pin1
  N13: R2.Pin_1, PXL/PWR.pin3
  N14: ADRSEL_HIGH.pin1, ADRSEL_HIGH.pin2, ADRSEL_HIGH.pin3, ADRSEL_HIGH.pin4, ADRSEL_HIGH.pin5, ADRSEL_HIGH.pin6, SWITCH.pin2, R3.Pin_0

notes:
  GND/SCL/SDA
  DIN/+5V/GND
  VCC/SIG
  1  2  4 8  16 32
